// Logisim project lc3.circ as structural Verilog: 16 circuits, main circuit main
module main (
  input  Reset,
  output out_2,
  output out_3,
  output out_4,
  output out_5,
  output out_6,
  output out_7,
  output out_8,
  output [15:0] out_9,
  output [15:0] out_10,
  output [15:0] out_11,
  output [15:0] out_12,
  output [15:0] out_13,
  output [15:0] out_14,
  output [15:0] out_15,
  output [15:0] out_16,
  output [15:0] out_17,
  output halt,
  output [15:0] out_19,
  output [15:0] out_20,
  output [15:0] out_21,
  output [15:0] out_22
);

  wire Arith, decodeir_1_writereg, getcst_1_usecst, or16_1_out_2, or16_2_out_2, ramctrl_1_memload,
       ramctrl_1_memstore;
  wire [1:0] LDI;
  wire [2:0] DR_SR, nzp_1_out_4;
  wire [15:0] ALU_Out, getcst_1_cst, LDI_LDR, load_store_1_reg_in, registres_1_out_sr1, registres_1_out_sr2;

  BiClock biclock_1 (.reset(Reset), .signal0(out_2), .signal1(out_3));
  RegPC regpc_1 (
    .H(out_3), .PC(out_9), .Reset(Reset), .IR(out_10), .R(registres_1_out_sr1), .TestNZP(out_5), .Jump(out_4));
  // Probe on out_9
  // Probe on out_11
  GetAddr getaddr_1 (
    .PC(out_9), .R(registres_1_out_sr1), .IR(out_10), .Addr(out_11), .Fetch(out_2), .LDI_STI_Value(LDI_LDR),
    .Execu(out_3), .LDI_STI(LDI));
  // Probe on out_12
  JSR_JSRR jsr_jsrr_1 (.DR_SR1(out_10[11:9]), .DR_SR2(DR_SR), .JMP(out_4));
  LED led_1 (.in(out_6));
  RamCtrl ramctrl_1 (
    .Store(out_7), .Fetch(out_2), .Exec(out_3), .Load(out_6), .MemStore(ramctrl_1_memstore),
    .MemLoad(ramctrl_1_memload), .LDI(LDI));
  LED led_2 (.in(out_7));
  LOAD_STORE load_store_1 (
    .Arith(Arith), .IR(out_10), .Adress(out_11), .Mem_OUT(out_13), .ALU_Out(ALU_Out),
    .Reg_In(load_store_1_reg_in), .JUMP(out_4));
  // Probe on out_13
  RAM #(.addrWidth(16), .dataWidth(16), .bus("separate")) ram_1 (
    .addr(out_11), .din(out_12), .data(out_13), .str(ramctrl_1_memstore), .clk(ramctrl_1_memstore),
    .ld(ramctrl_1_memload));  // open: sel, clr
  Register #(.width(16), .trigger("falling")) RegIR (.D(out_13), .Q(out_10), .clk(out_2));  // open: en, clr
  DecodeIR decodeir_1 (
    .IR(out_10), .Jump(out_4), .WriteReg(decodeir_1_writereg), .Load(out_6), .Store(out_7), .Arith(Arith),
    .LDI_STI(LDI));
  // Probe on DR_SR
  // Probe on out_10[8:6]
  // Probe on out_10[2:0]
  // Probe on getcst_1_cst
  GetCst getcst_1 (.IR(out_10), .Cst(getcst_1_cst), .UseCst(getcst_1_usecst));
  // Probe on out_10[15:14]
  and and_1 (out_8, decodeir_1_writereg, out_3);
  LDI_STI ldi_sti_1 (.MEMIN(out_13), .EXEC(out_3), .LDI_STI(LDI_LDR));
  Registres registres_1 (
    .SR1(out_10[8:6]), .IN(load_store_1_reg_in), .SR2(out_10[2:0]), .WriteReg(out_8), .DR_SR(DR_SR),
    .OUT_SR1(registres_1_out_sr1), .OUT_SR2(registres_1_out_sr2), .OUT_SR(out_12), .R0(out_14), .R1(out_15),
    .R2(out_16), .R3(out_17), .R4(out_19), .R5(out_20), .R6(out_21), .R7(out_22));
  // Probe on registres_1_out_sr1
  ALU alu_1 (
    .UseCst(getcst_1_usecst), .e2(out_10[15:14]), .Input1(registres_1_out_sr1), .Input2(registres_1_out_sr2),
    .Cst(getcst_1_cst), .Output(ALU_Out));
  // Probe on registres_1_out_sr2
  // Probe on ALU_Out
  NZP nzp_1 (.RES(load_store_1_reg_in), .IR(out_10), .TestNZP(out_5), .WriteReg(out_8), .out_4(nzp_1_out_4));
  // Probe on nzp_1_out_4
  Or16 or16_1 (.in_1(out_10), .out_2(or16_1_out_2));
  Or16 or16_2 (.in_1(out_9), .out_2(or16_2_out_2));
  // Probe on out_14
  // Probe on out_15
  // Probe on out_16
  // Probe on out_17
  // Probe on out_19
  // Probe on out_20
  // Probe on out_21
  // Probe on out_22
  and and_2 (halt, ~or16_1_out_2, or16_2_out_2);  // AND_Gate

  // Other names for the same wires on the sheet: Addr[15:0] = out_11; Condition = out_5; Exec = out_3; Fetch = out_2;
  //   IR[15:0] = out_10; DR_SR1[2:0] = out_10[11:9]; JumpInstr = out_4; Load = out_6; MemIN[15:0] = out_12;
  //   MemOUT[15:0] = out_13; PC[15:0] = out_9; R0[15:0] = out_14; R1[15:0] = out_15; R2[15:0] = out_16;
  //   R3[15:0] = out_17; R4[15:0] = out_19; R5[15:0] = out_20; R6[15:0] = out_21; R7[15:0] = out_22; Store = out_7;
  //   WriteReg = out_8

  // Notes on the sheet:
  //   R
  //   IR
  //   R
  //   IR
  //   RAM
  //   Traces (NE PAS MODIFIER)______________________________________________________________________________________________________
  //   GetOp
  //   Arret des traces au 1er NOP
endmodule

module ALU (
  input  [15:0] Input1,
  input  [15:0] Input2,
  input  [15:0] Cst,
  input  UseCst,
  input  [1:0] e2,
  output [15:0] Output
);

  wire [15:0] adder_1_out, and_1_out, multiplexer_1_out, xor_1_out;

  Multiplexer #(.width(16), .enable("false")) multiplexer_1 (
    .in0(Input2), .in1(Cst), .out(multiplexer_1_out), .sel(UseCst));
  Adder #(.width(16)) adder_1 (.a(multiplexer_1_out), .b(Input1), .out(adder_1_out));  // open: cin, cout
  assign and_1_out = Input1 & multiplexer_1_out;  // AND_Gate and_1, 16 bits wide
  Multiplexer #(.select(2), .width(16), .enable("false")) multiplexer_2 (
    .in0(adder_1_out), .in1(and_1_out), .in2(xor_1_out), .out(Output), .sel(e2));  // open: in3
  assign xor_1_out = multiplexer_1_out ^ Input1;  // XOR_Gate xor_1, 16 bits wide
endmodule

module BiClock (
  input  reset,
  output signal0,
  output signal1
);

  wire and_1_out, horloge_out, not_1_out, register_1_q;

  Clock horloge (.out(horloge_out));
  not not_1 (not_1_out, register_1_q);
  Register #(.width(1), .trigger("falling")) register_1 (
    .D(not_1_out), .Q(register_1_q), .clk(horloge_out), .clr(reset));  // open: en
  and and_1 (and_1_out, horloge_out, ~reset);  // AND_Gate
  and and_2 (signal0, ~register_1_q, and_1_out);  // AND_Gate
  and and_3 (signal1, register_1_q, and_1_out);

  // Notes on the sheet:
  //   Ce module divise une horloge en deux sous-horloges alternées
  //   Chronogrammes :
  //   horloge: 0101010101 signal0: 0100010001 signal1: 000100010
  //   registre 1-bit
  //   Enable
  //   select : 0 / 1
endmodule

module DecodeIR (
  input  [15:0] IR,
  output Jump,
  output WriteReg,
  output Arith,
  output Load,
  output Store,
  output [1:0] LDI_STI
);

  wire and_1_out, multiplexer_1_out, multiplexer_2_out;

  Demultiplexer #(.select(2), .enable("false")) demultiplexer_1 (
    .out0(Jump), .out1(Arith), .out2(Load), .out3(Store), .in(1'b1), .sel(IR[13:12]));
  Multiplexer #(.select(2), .enable("false")) multiplexer_1 (
    .in0(1'b0), .in1(1'b1), .in2(1'b0), .in3(1'b0), .out(multiplexer_1_out), .sel(IR[15:14]));
  Multiplexer #(.select(2), .enable("false")) multiplexer_2 (
    .in0(1'b0), .in1(1'b0), .in2(1'b1), .in3(1'b0), .out(multiplexer_2_out), .sel(IR[15:14]));
  and and_1 (and_1_out, multiplexer_1_out, Jump);
  and and_2 (LDI_STI[0], Load, multiplexer_2_out);
  or or_1 (WriteReg, and_1_out, Arith, Load);
  and and_3 (LDI_STI[1], Store, multiplexer_2_out);

  // Notes on the sheet:
  //   JSR/JSRR
  //   LDI/STI
endmodule

module GetAddr (
  input  [15:0] PC,
  input  Execu,
  input  [1:0] LDI_STI,
  input  Fetch,
  input  [15:0] LDI_STI_Value,
  input  [15:0] R,
  input  [15:0] IR,
  output [15:0] Addr
);

  wire and_1_out, or_1_out;
  wire [15:0] adder_2_out, adder_3_out, adder_4_out, adder_5_out, bit_extender_1_out, bit_extender_2_out,
       multiplexer_1_out, multiplexer_2_out, multiplexer_3_out, multiplexer_4_out, multiplexer_5_out,
       multiplexer_6_out, subtractor_1_out, subtractor_2_out;

  and and_1 (and_1_out, Execu, or_1_out);
  or or_1 (or_1_out, LDI_STI[0], LDI_STI[1]);
  Multiplexer #(.width(16), .disabled(0), .enable("false")) multiplexer_1 (
    .in0(bit_extender_1_out), .in1(adder_3_out), .out(multiplexer_1_out), .sel(bit_extender_1_out[8]));
  Adder #(.width(16)) adder_1 (.a(PC), .b(multiplexer_2_out), .out(Addr));  // open: cin, cout
  Multiplexer #(.width(16), .enable("false")) multiplexer_2 (
    .in0(multiplexer_3_out), .in1(subtractor_1_out), .out(multiplexer_2_out), .sel(and_1_out));
  Multiplexer #(.width(16), .enable("false")) multiplexer_3 (
    .in0(multiplexer_4_out), .in1({16{1'b0}}), .out(multiplexer_3_out), .sel(Fetch));
  Multiplexer #(.select(2), .width(16), .disabled(0), .enable("false")) multiplexer_4 (
    .in0({16{1'b0}}), .in1({16{1'b0}}), .in2(multiplexer_5_out), .in3(multiplexer_5_out),
    .out(multiplexer_4_out), .sel(IR[13:12]));
  Multiplexer #(.select(2), .width(16), .disabled(0), .enable("false")) multiplexer_5 (
    .in0(adder_2_out), .in1(subtractor_2_out), .in2(adder_2_out), .in3(adder_2_out), .out(multiplexer_5_out),
    .sel(IR[15:14]));
  Adder #(.width(16)) adder_2 (.a({16{1'b0}}), .b(multiplexer_1_out), .out(adder_2_out), .cin(1'b1));  // open: cout
  Adder #(.width(16)) adder_3 (.a(bit_extender_1_out), .b(16'hfe00), .out(adder_3_out));  // open: cin, cout
  assign bit_extender_1_out = {{7{1'b0}}, IR[8:0]};  // Bit_Extender bit_extender_1
  assign bit_extender_2_out = {{10{1'b0}}, IR[5:0]};  // Bit_Extender bit_extender_2
  Multiplexer #(.width(16), .disabled(0), .enable("false")) multiplexer_6 (
    .in0(bit_extender_2_out), .in1(adder_4_out), .out(multiplexer_6_out), .sel(bit_extender_2_out[5]));
  Adder #(.width(16)) adder_4 (.a(bit_extender_2_out), .b(16'hfdc0), .out(adder_4_out));  // open: cin, cout
  Subtractor #(.width(16)) subtractor_1 (.a(LDI_STI_Value), .b(PC), .out(subtractor_1_out));  // open: bin, bout
  Subtractor #(.width(16)) subtractor_2 (.a(adder_5_out), .b(PC), .out(subtractor_2_out));  // open: bin, bout
  // Probe on subtractor_2_out
  Adder #(.width(16)) adder_5 (.a(multiplexer_6_out), .b(R), .out(adder_5_out));  // open: cin, cout

  // Notes on the sheet:
  //   JMP/ARITH
  //   PC+1
  //   LOAD/STORE
  //   Offset9
  //   LDR/STR
  //   PC+Offset
  //   Positive/negative
  //   mem(pc+offset6)-pc
  //   (R+offset6)-PC 
  //   Offset6
  //   Positive/negative
  //   R+Offset6
endmodule

module GetCst (
  input  [15:0] IR,
  output [15:0] Cst,
  output UseCst
);

  assign Cst = {{11{IR[4]}}, IR[4:0]};  // Bit_Extender bit_extender_1

  assign UseCst = IR[5];
endmodule

module NZP (
  input  WriteReg,
  input  [15:0] RES,
  input  [15:0] IR,
  output [2:0] out_4,
  output TestNZP
);

  wire [2:0] and_1_out, comparator_1_lt;

  Comparator #(.width(16)) comparator_1 (
    .a({16{1'b0}}), .b(RES), .gt(comparator_1_lt[2]), .eq(comparator_1_lt[1]), .lt(comparator_1_lt[0]));
  Multiplexer #(.width(3), .enable("false")) multiplexer_1 (
    .in0(out_4), .in1(comparator_1_lt), .out(out_4), .sel(WriteReg));
  // Probe on IR[11:9]
  assign and_1_out = out_4 & IR[11:9];  // AND_Gate and_1, 3 bits wide
  or or_1 (TestNZP, and_1_out[0], and_1_out[1], and_1_out[2]);

  // Notes on the sheet:
  //   (Resultat du calcul courant)
  //   (Instruction courante)
  //   (Instruction mettant à jour NZP)
endmodule

// Off6
module Offset6 (
  input  [15:0] IR,
  output [15:0] Off6
);

  assign Off6 = {{10{IR[5]}}, IR[5:0]};  // Bit_Extender bit_extender_1
endmodule

// Off9
module Offset9 (
  input  [15:0] IR,
  output [15:0] Off9
);

  assign Off9 = {{7{IR[8]}}, IR[8:0]};  // Bit_Extender bit_extender_1
endmodule

module Or16 (
  input  [15:0] in_1,
  output out_2
);

  wire [3:0] or_1_out;

  assign or_1_out = in_1[3:0] | in_1[7:4] | in_1[11:8] | in_1[15:12];  // OR_Gate or_1, 4 bits wide
  or or_2 (out_2, or_1_out[0], or_1_out[1], or_1_out[2], or_1_out[3]);
endmodule

module RamCtrl (
  input  Exec,
  input  Fetch,
  input  Load,
  input  [1:0] LDI,
  input  Store,
  output MemLoad,
  output MemStore
);

  wire and_1_out, and_2_out, not_1_out, or_1_out, or_2_out;

  and and_1 (and_1_out, Exec, Load);
  and and_2 (and_2_out, Exec, Store);
  not not_1 (not_1_out, or_1_out);
  or or_1 (or_1_out, Exec, Fetch);
  or or_2 (or_2_out, Fetch, and_1_out);
  Multiplexer #(.enable("false")) multiplexer_1 (.in0(and_2_out), .in1(not_1_out), .out(MemStore), .sel(LDI[1]));
  or or_3 (MemLoad, or_2_out, LDI[1], LDI[0]);
endmodule

module Registres (
  input  [2:0] SR1,
  input  [15:0] IN,
  input  [2:0] SR2,
  input  WriteReg,
  input  [2:0] DR_SR,
  output [15:0] R0,
  output [15:0] OUT_SR1,
  output [15:0] R1,
  output [15:0] R2,
  output [15:0] R3,
  output [15:0] OUT_SR2,
  output [15:0] R4,
  output [15:0] R5,
  output [15:0] OUT_SR,
  output [15:0] R6,
  output [15:0] R7
);

  wire decoder_1_out0, decoder_1_out1, decoder_1_out2, decoder_1_out3, decoder_1_out4, decoder_1_out5,
       decoder_1_out6, decoder_1_out7;

  Decoder #(.select(3), .disabled(0)) decoder_1 (
    .out0(decoder_1_out0), .out1(decoder_1_out1), .out2(decoder_1_out2), .out3(decoder_1_out3),
    .out4(decoder_1_out4), .out5(decoder_1_out5), .out6(decoder_1_out6), .out7(decoder_1_out7), .sel(DR_SR),
    .en(WriteReg));
  Register #(.width(16), .trigger("falling")) u_R0 (.D(IN), .Q(R0), .clk(decoder_1_out0));  // open: en, clr
  Register #(.width(16), .trigger("falling")) u_R1 (.D(IN), .Q(R1), .clk(decoder_1_out1));  // open: en, clr
  Register #(.width(16), .trigger("falling")) u_R2 (.D(IN), .Q(R2), .clk(decoder_1_out2));  // open: en, clr
  Register #(.width(16), .trigger("falling")) u_R3 (.D(IN), .Q(R3), .clk(decoder_1_out3));  // open: en, clr
  Register #(.width(16), .trigger("falling")) u_R4 (.D(IN), .Q(R4), .clk(decoder_1_out4));  // open: en, clr
  Register #(.width(16), .trigger("falling")) u_R5 (.D(IN), .Q(R5), .clk(decoder_1_out5));  // open: en, clr
  Register #(.width(16), .trigger("falling")) u_R6 (.D(IN), .Q(R6), .clk(decoder_1_out6));  // open: en, clr
  Register #(.width(16), .trigger("falling")) u_R7 (.D(IN), .Q(R7), .clk(decoder_1_out7));  // open: en, clr
  Multiplexer #(.select(3), .width(16), .enable("false")) multiplexer_1 (
    .in0(R0), .in1(R1), .in2(R2), .in3(R3), .in4(R4), .in5(R5), .in6(R6), .in7(R7), .out(OUT_SR1), .sel(SR1));
  Multiplexer #(.select(3), .width(16), .enable("false")) multiplexer_2 (
    .in0(R0), .in1(R1), .in2(R2), .in3(R3), .in4(R4), .in5(R5), .in6(R6), .in7(R7), .out(OUT_SR2), .sel(SR2));
  Multiplexer #(.select(3), .width(16), .enable("false")) multiplexer_3 (
    .in0(R0), .in1(R1), .in2(R2), .in3(R3), .in4(R4), .in5(R5), .in6(R6), .in7(R7), .out(OUT_SR), .sel(DR_SR));
endmodule

module RegPC (
  input  Jump,
  input  H,
  input  Reset,
  input  TestNZP,
  input  [15:0] R,
  input  [15:0] IR,
  output [15:0] PC
);

  wire [15:0] adder_1_out, adder_2_out, adder_3_out, bit_extender_1_out, bit_extender_2_out,
       multiplexer_1_out, multiplexer_2_out, multiplexer_3_out, multiplexer_4_out, multiplexer_5_out,
       multiplexer_6_out, subtractor_1_out;

  assign bit_extender_1_out = {{7{1'b0}}, IR[8:0]};  // Bit_Extender bit_extender_1
  // Probe on multiplexer_1_out
  Multiplexer #(.width(16), .disabled(0), .enable("false")) multiplexer_1 (
    .in0({16{1'b0}}), .in1(multiplexer_2_out), .out(multiplexer_1_out), .sel(Jump));
  Multiplexer #(.select(2), .width(16), .disabled(0), .enable("false")) multiplexer_2 (
    .in0(multiplexer_3_out), .in1(multiplexer_5_out), .in2({16{1'b0}}), .in3(subtractor_1_out),
    .out(multiplexer_2_out), .sel(IR[15:14]));
  Multiplexer #(.width(16), .disabled(0), .enable("false")) multiplexer_3 (
    .in0({16{1'b0}}), .in1(multiplexer_4_out), .out(multiplexer_3_out), .sel(TestNZP));
  Multiplexer #(.width(16), .disabled(0), .enable("false")) multiplexer_4 (
    .in0(bit_extender_1_out), .in1(adder_1_out), .out(multiplexer_4_out), .sel(bit_extender_1_out[8]));
  Adder #(.width(16)) adder_1 (.a(bit_extender_1_out), .b(16'hfe00), .out(adder_1_out));  // open: cin, cout
  // Probe on multiplexer_1_out
  // Probe on multiplexer_5_out
  Multiplexer #(.width(16), .disabled(0), .enable("false")) multiplexer_5 (
    .in0(subtractor_1_out), .in1(multiplexer_6_out), .out(multiplexer_5_out), .sel(IR[11]));
  Multiplexer #(.width(16), .disabled(0), .enable("false")) multiplexer_6 (
    .in0(bit_extender_2_out), .in1(adder_3_out), .out(multiplexer_6_out), .sel(bit_extender_2_out[10]));
  assign bit_extender_2_out = {{5{1'b0}}, IR[10:0]};  // Bit_Extender bit_extender_2
  Subtractor #(.width(16)) subtractor_1 (.a(R), .b(PC), .out(subtractor_1_out), .bin(1'b1));  // open: bout
  Adder #(.width(16)) adder_2 (.a(PC), .b(multiplexer_1_out), .out(adder_2_out), .cin(1'b1));  // open: cout
  Adder #(.width(16)) adder_3 (.a(bit_extender_2_out), .b(16'hf800), .out(adder_3_out));  // open: cin, cout
  Register #(.width(16), .trigger("falling")) u_PC (.D(adder_2_out), .Q(PC), .clk(H), .clr(Reset));  // open: en

  // Notes on the sheet:
  //   POS/NEG
  //   BRnzp
  //   Offset9
  //   JMP
  //   JSR/JSRR
  //   JSR/JSRR
  //   JSR
  //   JSRR
  //   R-PC
  //   POS/NEG
  //   PC <- PC + 1
endmodule

// REGIN
module LOAD_STORE (
  input  JUMP,
  input  [15:0] Mem_OUT,
  input  [15:0] Adress,
  input  Arith,
  input  [15:0] IR,
  input  [15:0] ALU_Out,
  output [15:0] Reg_In
);

  wire [15:0] adder_1_out, multiplexer_1_out, multiplexer_2_out;

  Multiplexer #(.select(2), .width(16), .enable("false")) multiplexer_1 (
    .in0(Mem_OUT), .in1(Mem_OUT), .in2(Mem_OUT), .in3(Adress), .out(multiplexer_1_out), .sel(IR[15:14]));
  Adder #(.width(16)) adder_1 (.a(Adress), .b({16{1'b0}}), .out(adder_1_out), .cin(1'b1));  // open: cout
  Multiplexer #(.width(16), .enable("false")) multiplexer_2 (
    .in0(multiplexer_1_out), .in1(adder_1_out), .out(multiplexer_2_out), .sel(JUMP));
  Multiplexer #(.width(16), .enable("false")) multiplexer_3 (
    .in0(multiplexer_2_out), .in1(ALU_Out), .out(Reg_In), .sel(Arith));

  // Notes on the sheet:
  //   LEA
  //   LOAD/STORE
  //   JSR/JSRR
  //   Arithm
endmodule

module JSR_JSRR (
  input  [2:0] DR_SR1,
  input  JMP,
  output [2:0] DR_SR2
);

  Multiplexer #(.width(3), .disabled(0), .enable("false")) multiplexer_1 (
    .in0(DR_SR1), .in1(3'b111), .out(DR_SR2), .sel(JMP));
endmodule

module LDI_STI (
  input  [15:0] MEMIN,
  input  EXEC,
  output [15:0] LDI_STI
);

  Register #(.width(16)) register_1 (.D(MEMIN), .Q(LDI_STI), .clk(EXEC));  // open: en, clr
endmodule
